# Fritzing sketch ElectronicsLayout (saved by Fritzing 0.9.3b)
breadboards: 1

parts:
  Part1 = Arduino Uno (Rev3)
  LED1 = LED - 5mm [color="Green (555nm)" package="5 mm [THT]"]
  LED2 = LED - 5mm [color="Red (633nm)" package="5 mm [THT]"]
  S1 = Toggle Switch [package=THT]  # not connected

nets:
  N1: Part1.D11_PWM/MOSI, LED2.cathode
  N2: Part1.D12/MISO, LED1.cathode
